# Fritzing sketch FinalPrototype (saved by Fritzing 0.9.3b)
breadboards: 1

parts:
  LED1 = LED - 5mm [color="Red (633nm)" package="5 mm [THT]"]
  R2 = Resistor [tolerance=±5% resistance=220 package=THT]
  Part1 = SparkFun ESP8266 Thing
  Q1 = NPN-Transistor [package="TO92 [THT]"]
  R3 = Resistor [tolerance=±5% resistance=220 package=THT]
  S1 = Pushbutton [package="[THT]"]
  R4 = Resistor [tolerance=±5% resistance=220 package=THT]

nets:
  N1: LED1.cathode, Part1.GPIO0
  N2: LED1.anode, R2.Pin_0
  N3: R2.Pin_1, Part1.GND, R3.Pin_1, R4.Pin_1
  N4: Part1.VCC, S1.Pin_3, S1.Pin_4
  N5: Part1.GPIO5, S1.Pin_1, S1.Pin_2, R4.Pin_0
  N6: Part1.GPIO13, Q1.E
  N7: Part1.ADC, Q1.C, R3.Pin_0
