# Fritzing sketch InitialPrototype (saved by Fritzing 0.9.3b)
breadboards: 1

parts:
  LED1 = LED - 5mm [color="Red (633nm)" package="5 mm [THT]"]
  R2 = Resistor [tolerance=±5% resistance=220 package=THT]
  Part1 = SparkFun ESP8266 Thing
  R3 = Rotary Potentiometer (Small) [maximum_resistance=100kΩ package=THT]

nets:
  N1: LED1.cathode, Part1.GPIO5
  N2: LED1.anode, R2.Pin_0
  N3: R2.Pin_1, Part1.GND, R3.leg2
  N4: Part1.VCC, R3.leg1
  N5: Part1.ADC, R3.wiper
