# Fritzing sketch TaskWifiPrototyp (saved by Fritzing 0.9.3b)
breadboards: 1

parts:
  Part1 = SparkFun ESP8266 Thing
  R4 = Resistor [tolerance=±5% resistance=220 package=THT]
  S1 = Pushbutton [package="[THT]"]

nets:
  N1: Part1.VCC, S1.Pin_1, S1.Pin_2
  N2: Part1.GND, R4.Pin_0
  N3: Part1.GPIO5, R4.Pin_1, S1.Pin_3, S1.Pin_4
